# Fritzing sketch DiagramaConex (saved by Fritzing 0.9.3b)

parts:
  J1 = STM32 Nucleo boards
  Arduino_CNC_Shield_V3_00_1 = Arduino_CNC_V3.00
  M2 = Stepper Motor - Bipolar
  A2 = AS5600 module
  A3 = AS5600 module
  Componente1 = Adafruit TCA9548A
  L1 = Solenoid  # not connected
  R1 = Resistor [tolerance=±5% resistance=100 package="0805 [SMD]"]
  Q1 = npn-Powertransistor [package="TO220 [THT]"]
  M3 = Stepper Motor - Bipolar
  M4 = Stepper Motor - Bipolar
  Power_plug1 = Power plug
  R2 = Resistor [tolerance=±5% resistance=4.7k package="0805 [SMD]"]
  R3 = Resistor [tolerance=±5% resistance=4.7k package="0805 [SMD]"]
  R4 = Resistor [tolerance=±5% resistance=4.7k package="0805 [SMD]"]
  R5 = Resistor [tolerance=±5% resistance=4.7k package="0805 [SMD]"]
  R6 = Resistor [tolerance=±5% resistance=4.7k package="0805 [SMD]"]
  R7 = Resistor [tolerance=±5% resistance=4.7k package="0805 [SMD]"]
  A4 = AS5600 module

nets:
  N1: J1.3v3, A4.Pin_1
  5V: J1.5V, Componente1.VCC
  GND: J1.GND, A2.Pin_3, A3.Pin_3, Componente1.GND, Componente1.A0, Componente1.A1, Componente1.A2, Q1.emitter, A4.Pin_3
  N2: J1.JP5_03, Arduino_CNC_Shield_V3_00_1.X_-_M0
  N3: J1.PB8, Componente1.INPUTSCL
  N4: J1.PB9, Componente1.INPUTSDA
  N5: J1.PC3, R1.Pin_1
  N6: Arduino_CNC_Shield_V3_00_1.POWER_-, Power_plug1.VCC
  N7: Arduino_CNC_Shield_V3_00_1.POWER_+, Power_plug1.GND
  N8: Arduino_CNC_Shield_V3_00_1.X-MTR_'1', M3.D
  N9: Arduino_CNC_Shield_V3_00_1.X-MTR_'2', M3.B
  N10: Arduino_CNC_Shield_V3_00_1.X-MTR_'3', M3.C
  N11: Arduino_CNC_Shield_V3_00_1.X-MTR_'4', M3.A
  N12: Arduino_CNC_Shield_V3_00_1.Z-MTR_'1', M2.D
  N13: Arduino_CNC_Shield_V3_00_1.Z-MTR_'2', M2.B
  N14: Arduino_CNC_Shield_V3_00_1.Z-MTR_'3', M2.C
  N15: Arduino_CNC_Shield_V3_00_1.Z-MTR_'4', M2.A
  N16: Arduino_CNC_Shield_V3_00_1.Y-MTR_'1', M4.D
  N17: Arduino_CNC_Shield_V3_00_1.Y-MTR_'2', M4.B
  N18: Arduino_CNC_Shield_V3_00_1.Y-MTR_'3', M4.C
  N19: Arduino_CNC_Shield_V3_00_1.Y-MTR_'4', M4.A
  N20: A2.Pin_1, R2.Pin_0, R3.Pin_0, R4.Pin_0, R5.Pin_0, R7.Pin_0
  N21: A2.Pin_5, Componente1.1SDA, R4.Pin_1
  N22: A2.Pin_6, Componente1.1SCL, R5.Pin_1
  N23: A3.Pin_1, R6.Pin_0
  N24: A3.Pin_5, Componente1.2SCL, R6.Pin_1
  N25: A3.Pin_6, Componente1.2SDA, R7.Pin_1
  N26: Componente1.0SDA, R2.Pin_1, A4.Pin_5
  N27: Componente1.0SCL, R3.Pin_1, A4.Pin_6

custom parts:
  Arduino_CNC_V3.00: Protoneer Arduino CNC Shield V3.00 If using Grbl V0.9: The “A” axis can not be used (yet). The “SCL” (Arduino A5) pin is now used for 'Probing' input. The “End Stops Z+ & Z-” (Arduino D11) and “SpnEn” (Arduino D12) have been switched!
  AS5600 module: .This module is mainly placed behind the stepper motor to obtain the rotation angle of the stepper motor.
  Adafruit TCA9548A: You just found the perfect I2C sensor, and you want to wire up two or three or more of them to your Arduino when you realize "Uh oh, this chip has a fixed I2C address, and from what I know about I2C, you cannot have two devices with the same address on the same SDA/SCL pins!" Are you out of luck? You would be, if you didn't have this ultra-cool TCA9548A 1-to-8 I2C multiplexer! Finally, a way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
