# Fritzing sketch electroiman (saved by Fritzing 0.9.3b)
circuit board: 4.51789cm x 2.52503cm
breadboards: 1

parts:
  D1 = Diode [package=diode-1n4148]
  J1 = Screw terminal - 2 pins [package=THT]
  J2 = Screw terminal - 2 pins [package=THT]
  J3 = Screw terminal - 2 pins [package=THT]
  C1 = Electrolytic Capacitor [capacitance=0.1mF package="100 mil [THT, electrolytic]"]
  Q2 = npn-Powertransistor [package="TO220 [THT]"]
  Q3 = MOSFET-NCHANNEL [package=to220v]
  R4 = Resistor [tolerance=±5% resistance=10k package=THT]
  R5 = Resistor [tolerance=±5% resistance=330 package=THT]
  R6 = Resistor [tolerance=±5% resistance=47k package=THT]

nets:
  N1: D1.A, J2.pin1, Q3.D
  N2: D1.C, J1.pin2, J2.pin2, C1.+, R6.Pin_1
  N3: J1.pin1, J3.pin1, C1.-, Q2.emitter, Q3.S
  N4: J3.pin2, R4.Pin_0
  N5: Q2.base, R4.Pin_1
  N6: Q2.collector, R5.Pin_0, R6.Pin_0
  N7: Q3.G, R5.Pin_1
